# Fritzing sketch SSR (saved by Fritzing 0.9.3b)
breadboards: 1

parts:
  S202S02 = RELAY-SOLIDSTATE [package=relay-s108t02]
  S02K275 = V18ZA2P [package=v18za2p]
  LED1 = LED - 3mm [color="Green (555nm)" package="3 mm [THT]"]
  U1 = PCF8574 [package="DIP16 [THT]"]
  R1 = Resistor [tolerance=±5% resistance=220 package=THT]
  Raspberry_Pi1 = Raspberry Pi 2
  L-in_|_L-out_|_N = screw terminal, 5 pins

nets:
  N1: S202S02.T1, L-in_|_L-out_|_N.pin1
  N2: S202S02.T2, S02K275.P$1, L-in_|_L-out_|_N.pin3
  VCC: S202S02.+, U1.VCC, Raspberry_Pi1.5V
  N3: S202S02.-, LED1.anode
  N4: S02K275.P$2, L-in_|_L-out_|_N.pin5
  N5: LED1.cathode, R1.Pin_1
  N6: U1.P0, R1.Pin_0
  GND: U1.GND, Raspberry_Pi1.GND
  N7: U1.SCL, Raspberry_Pi1.ID_SC
  N8: U1.SDA, Raspberry_Pi1.ID_SD
